// Logisim project 32Bit_IndirectAddressing_3AddressFormat.circ as structural Verilog: 11 circuits, main circuit main
module main (
  input  [8:0] PC_in,
  input  PcReset,
  input  CLOCK,
  output CARRY,
  output NEGETIVE,
  output OVERFLOW,
  output POSTIVE,
  output ZERO,
  output EVEN_PARITY,
  output ODD_PARITY,
  output [19:0] MDR_OUT,
  output [19:0] IR_OUT,
  output [8:0] MAR_OUT,
  output [15:0] RA,
  output [8:0] PC_OUT,
  output [19:0] IR_BUFF,
  output [15:0] RB,
  output [31:0] RZ,
  output [31:0] ALU_OUT,
  output [15:0] REG_FILE_OUT,
  output [15:0] TEMP_REG_DM,
  output [15:0] DATA_MEMORY,
  output [19:0] RB_2
);

  wire and_1_out, and_2_out, load_exchange_1_load_exchangeop, nor_1_out, not_1_out, not_2_out, not_3_out,
       or_1_out, or_2_out, or_3_out, register_1_q, shift_register_1_out, shift_register_2_out,
       shift_register_3_out, shift_register_3_q0, shift_register_4_out, shift_register_4_q0,
       shift_register_4_q6, shift_register_5_out, shift_register_6_out, shift_register_6_q2,
       storecmp_1_storeop;
  wire [3:0] multiplexer_2_out, multiplexer_3_out;
  wire [7:0] bit_extender_1_out, multiplexer_1_out;
  wire [15:0] bit_extender_2_out;

  Shift_Register #(.length(5)) shift_register_1 (
    .in(shift_register_1_out), .clk(CLOCK), .out(shift_register_1_out));  // open: shift, load, clr, d0, q0, d1, q1, d2, q2, d3, q3, d4, q4
  or or_1 (or_1_out, not_1_out, shift_register_3_out);
  Shift_Register #(.length(10)) shift_register_2 (
    .in(shift_register_2_out), .clk(CLOCK), .out(shift_register_2_out));  // open: shift, load, clr, d0, q0, d1, q1, d2, q2, d3, q3, d4, q4, d5, q5, d6, q6, d7, q7, d8, q8, d9, q9
  Shift_Register #(.length(10)) shift_register_3 (
    .in(shift_register_3_out), .clk(CLOCK), .out(shift_register_3_out), .q0(shift_register_3_q0));  // open: shift, load, clr, d0, d1, q1, d2, q2, d3, q3, d4, q4, d5, q5, d6, q6, d7, q7, d8, q8, d9, q9
  Bit_Extender #(.in_width(16), .out_width(8)) bit_extender_1 (.in(TEMP_REG_DM), .out(bit_extender_1_out));
  Register #(.width(1)) register_1 (.D(1'b1), .Q(register_1_q), .clk(CLOCK));  // open: en, clr
  Shift_Register #(.length(10)) shift_register_4 (
    .in(shift_register_4_out), .clk(CLOCK), .out(shift_register_4_out), .q0(shift_register_4_q0),
    .q6(shift_register_4_q6));  // open: shift, load, clr, d0, d1, q1, d2, q2, d3, q3, d4, q4, d5, q5, d6, d7, q7, d8, q8, d9, q9
  Multiplexer #(.width(8)) multiplexer_1 (
    .in0(IR_OUT[7:0]), .in1(bit_extender_1_out), .out(multiplexer_1_out), .sel(or_1_out));  // open: en
  and and_1 (and_1_out, shift_register_3_q0, register_1_q);
  pc pc_1 (.PcEnable(shift_register_2_out), .PC_IN(PC_in), .CLOCK(CLOCK), .pcReset(PcReset), .PC_OUT(PC_OUT));
  ROM #(.addrWidth(9), .dataWidth(20)) rom_1 (.addr(MAR_OUT), .data(RB_2));  // open: sel
  not not_1 (not_1_out, or_3_out);
  Register #(.width(20)) MDR (.D(RB_2), .en(shift_register_4_q0), .Q(MDR_OUT), .clk(CLOCK), .clr(PcReset));
  storeCmp storecmp_1 (.OPCODE(IR_OUT[19:16]), .storeOP(storecmp_1_storeop));
  Bit_Extender #(.in_width(32)) bit_extender_2 (.in(RZ), .out(bit_extender_2_out));
  Shift_Register #(.length(10)) shift_register_5 (
    .in(shift_register_1_out), .clk(CLOCK), .out(shift_register_5_out));  // open: shift, load, clr, d0, q0, d1, q1, d2, q2, d3, q3, d4, q4, d5, q5, d6, q6, d7, q7, d8, q8, d9, q9
  Register #(.width(9)) MAR (.D(PC_OUT), .en(shift_register_4_out), .Q(MAR_OUT), .clk(CLOCK), .clr(PcReset));
  RAM #(.dataWidth(16), .bus("separate")) ram_1 (
    .addr(multiplexer_1_out), .din(RB), .data(DATA_MEMORY), .str(not_1_out), .sel(1'b1), .clk(CLOCK),
    .ld(or_3_out));  // open: clr
  Register #(.width(16)) u_RA (.D(TEMP_REG_DM), .en(and_1_out), .Q(RA), .clk(CLOCK));  // open: clr
  or or_2 (or_2_out, storecmp_1_storeop, shift_register_5_out);
  load_exchange load_exchange_1 (.OPCODE(IR_OUT[19:16]), .load_exchangeOP(load_exchange_1_load_exchangeop));
  Register #(.width(20)) IR (.D(MDR_OUT), .en(shift_register_4_q6), .Q(IR_OUT), .clk(CLOCK), .clr(PcReset));
  Register #(.width(16)) tempReg (.D(DATA_MEMORY), .en(1'b1), .Q(TEMP_REG_DM), .clk(CLOCK));  // open: clr
  alu ALU (.INPUT_A(RB), .INPUT_B(RA), .OPCODE(IR_OUT[19:16]), .RESULT(ALU_OUT));
  register_file register_file_1 (
    .INPUT(bit_extender_2_out), .SELECT(multiplexer_3_out), .R_W_prime(or_2_out), .CLOCK(CLOCK),
    .OUTPUT(REG_FILE_OUT));
  Register #(.width(20)) IRBuff (.D(IR_OUT), .en(shift_register_6_q2), .Q(IR_BUFF), .clk(CLOCK), .clr(PcReset));
  Shift_Register #(.length(5)) shift_register_6 (
    .in(shift_register_6_out), .clk(CLOCK), .out(shift_register_6_out), .q2(shift_register_6_q2));  // open: shift, load, clr, d0, q0, d1, q1, d2, d3, q3, d4, q4
  Register #(.width(16)) u_RB (.D(REG_FILE_OUT), .en(and_1_out), .Q(RB), .clk(CLOCK));  // open: clr
  Multiplexer #(.width(4), .enable("false")) multiplexer_2 (
    .in0(IR_OUT[15:12]), .in1(IR_BUFF[15:12]), .out(multiplexer_2_out), .sel(shift_register_6_out));
  Register #(.width(32)) u_Rz (.D(ALU_OUT), .en(1'b1), .Q(RZ), .clk(CLOCK));  // open: clr
  not not_2 (not_2_out, load_exchange_1_load_exchangeop);
  PSW psw_1 (
    .INPUT(ALU_OUT), .CARRY(CARRY), .NEGATIVE(NEGETIVE), .OVERFLOW(OVERFLOW), .POSITIVE(POSTIVE),
    .ZERO(ZERO), .EVEN_PARITY(EVEN_PARITY), .ODD_PARITY(ODD_PARITY));
  nor nor_1 (nor_1_out, storecmp_1_storeop, not_3_out);
  Multiplexer #(.width(4), .enable("false")) multiplexer_3 (
    .in0(multiplexer_2_out), .in1(IR_OUT[11:8]), .out(multiplexer_3_out), .sel(nor_1_out));
  or or_3 (or_3_out, not_2_out, shift_register_5_out);
  not not_3 (not_3_out, and_2_out);
  and and_2 (and_2_out, shift_register_5_out, not_2_out);

  // Other names for the same wires on the sheet: CM[19:0] = RB_2; DM[15:0] = DATA_MEMORY;
  //   TEMP_REG__dm[15:0] = TEMP_REG_DM

  // Notes on the sheet:
  //   000100010
  //   PC shiftRegister
  //   Indirect Addressing shiftRegister
  //   100001000
  //   CODE MEMEORY
  //   000010001
  //   MAR shiftRegister
  //   contents of rom_1 (hex, n*v repeats v):
  //   9f200 1ff00 df300 1ff02
  //   DATA MEMEORY
  //   DATA FROM MEM
  //   REG R/W` shift
  //   1101111011
  //   DATA FROM REGISTER
  //   RESULT
endmodule

// ALU
module alu (
  input  [15:0] INPUT_A,
  input  [15:0] INPUT_B,
  input  [3:0] OPCODE,
  output [31:0] RESULT
);

  wire adder_1_cout, adder_2_cout, subtractor_1_bout, subtractor_2_bout;
  wire [3:0] bit_extender_1_out;
  wire [15:0] adder_1_out, adder_2_out, and_1_out, bit_extender_3_out, bit_extender_4_out,
       bit_extender_5_out, divider_1_out, divider_1_rem, multiplier_1_cout, multiplier_1_out, not_1_out,
       or_1_out, shifter_1_out, shifter_2_out, shifter_3_out, shifter_4_out, subtractor_1_out,
       subtractor_2_out, undriven;
  wire [31:0] bit_extender_2_out, bit_extender_7_out, bit_extender_8_out, bit_extender_9_out,
       bit_extender_10_out, bit_extender_11_out, bit_extender_12_out, bit_extender_13_out;

  Hex_Digit_Display hex_digit_display_1 (.value(INPUT_A[15:12]));  // open: dp
  Hex_Digit_Display hex_digit_display_2 (.value(INPUT_B[15:12]));  // open: dp
  Hex_Digit_Display hex_digit_display_3 (.value(INPUT_A[11:8]));  // open: dp
  Hex_Digit_Display hex_digit_display_4 (.value(INPUT_A[7:4]));  // open: dp
  Hex_Digit_Display hex_digit_display_5 (.value(INPUT_B[11:8]));  // open: dp
  Hex_Digit_Display hex_digit_display_6 (.value(INPUT_B[7:4]));  // open: dp
  Hex_Digit_Display hex_digit_display_7 (.value(INPUT_A[3:0]));  // open: dp
  Hex_Digit_Display hex_digit_display_8 (.value(INPUT_B[3:0]));  // open: dp
  Bit_Extender #(.in_width(16), .out_width(4)) bit_extender_1 (.in(INPUT_A), .out(bit_extender_1_out));
  assign bit_extender_2_out = {{16{1'b0}}, INPUT_B};  // Bit_Extender bit_extender_2
  Adder #(.width(16)) adder_1 (.a(INPUT_A), .b(INPUT_B), .out(adder_1_out), .cout(adder_1_cout));  // open: cin
  Subtractor #(.width(16)) subtractor_1 (
    .a(INPUT_A), .b(INPUT_B), .out(subtractor_1_out), .bout(subtractor_1_bout));  // open: bin
  Multiplier #(.width(16)) multiplier_1 (
    .a(INPUT_A), .b(INPUT_B), .out(multiplier_1_out), .cout(multiplier_1_cout));  // open: cin
  Divider #(.width(16)) divider_1 (.a(INPUT_A), .b(INPUT_B), .out(divider_1_out), .rem(divider_1_rem));  // open: upper
  Adder #(.width(16)) adder_2 (.a(INPUT_A), .b(16'h1), .out(adder_2_out), .cout(adder_2_cout));  // open: cin
  Subtractor #(.width(16)) subtractor_2 (
    .a(INPUT_A), .b(16'h1), .out(subtractor_2_out), .bout(subtractor_2_bout));  // open: bin
  assign and_1_out = INPUT_A & INPUT_B;  // AND_Gate and_1, 16 bits wide
  assign or_1_out = INPUT_A | INPUT_B;  // OR_Gate or_1, 16 bits wide
  assign not_1_out = ~INPUT_A;  // NOT_Gate not_1, 16 bits wide
  Shifter #(.width(16), .shift("lr")) shifter_1 (.in(INPUT_B), .\dist (bit_extender_1_out), .out(shifter_1_out));
  Shifter #(.width(16)) shifter_2 (.in(INPUT_B), .\dist (bit_extender_1_out), .out(shifter_2_out));
  Shifter #(.width(16), .shift("rr")) shifter_3 (.in(INPUT_B), .\dist (bit_extender_1_out), .out(shifter_3_out));
  Shifter #(.width(16), .shift("rl")) shifter_4 (.in(INPUT_B), .\dist (bit_extender_1_out), .out(shifter_4_out));
  assign bit_extender_3_out = {{15{1'b0}}, adder_1_cout};  // Bit_Extender bit_extender_3
  assign bit_extender_4_out = {{15{1'b0}}, subtractor_1_bout};  // Bit_Extender bit_extender_4
  assign bit_extender_5_out = {{15{1'b0}}, adder_2_cout};  // Bit_Extender bit_extender_5
  Bit_Extender #(.in_width(1)) bit_extender_6 (.in(subtractor_2_bout));  // open: out
  assign bit_extender_7_out = {{16{1'b0}}, and_1_out};  // Bit_Extender bit_extender_7
  assign bit_extender_8_out = {{16{1'b0}}, or_1_out};  // Bit_Extender bit_extender_8
  assign bit_extender_9_out = {{16{1'b0}}, not_1_out};  // Bit_Extender bit_extender_9
  assign bit_extender_10_out = {{16{1'b0}}, shifter_1_out};  // Bit_Extender bit_extender_10
  assign bit_extender_11_out = {{16{1'b0}}, shifter_2_out};  // Bit_Extender bit_extender_11
  assign bit_extender_12_out = {{16{1'b0}}, shifter_3_out};  // Bit_Extender bit_extender_12
  assign bit_extender_13_out = {{16{1'b0}}, shifter_4_out};  // Bit_Extender bit_extender_13
  Multiplexer #(.select(4), .width(32), .enable("false")) multiplexer_1 (
    .in0(bit_extender_2_out), .in1(bit_extender_2_out), .in2({bit_extender_3_out, adder_1_out}),
    .in3({bit_extender_4_out, subtractor_1_out}), .in4({multiplier_1_cout, multiplier_1_out}),
    .in5({divider_1_rem, divider_1_out}), .in6({bit_extender_5_out, adder_2_out}),
    .in7({undriven, subtractor_2_out}), .in8(bit_extender_7_out), .in9(bit_extender_8_out),
    .in10(bit_extender_9_out), .in11(bit_extender_2_out), .in12(bit_extender_10_out),
    .in13(bit_extender_11_out), .in14(bit_extender_12_out), .in15(bit_extender_13_out), .out(RESULT),
    .sel(OPCODE));
endmodule

// REG FILE
module register_file (
  input  [15:0] INPUT,
  input  R_W_prime,
  input  [3:0] SELECT,
  input  CLOCK,
  output [15:0] OUTPUT
);

  wire decoder_1_out0, decoder_1_out1, decoder_1_out2, decoder_1_out3, decoder_1_out4, decoder_1_out5,
       decoder_1_out6, decoder_1_out7, decoder_1_out8, decoder_1_out9, decoder_1_out10, decoder_1_out11,
       decoder_1_out12, decoder_1_out13, decoder_1_out14, decoder_1_out15, not_1_out;
  wire [15:0] register_1_q, register_2_q, register_3_q, register_4_q, register_5_q, register_6_q,
       register_7_q, register_8_q, register_9_q, register_10_q, register_11_q, register_12_q, register_13_q,
       register_14_q, register_15_q, register_16_q;

  not not_1 (not_1_out, R_W_prime);
  Decoder #(.select(4), .disabled(0)) decoder_1 (
    .out0(decoder_1_out0), .out1(decoder_1_out1), .out2(decoder_1_out2), .out3(decoder_1_out3),
    .out4(decoder_1_out4), .out5(decoder_1_out5), .out6(decoder_1_out6), .out7(decoder_1_out7),
    .out8(decoder_1_out8), .out9(decoder_1_out9), .out10(decoder_1_out10), .out11(decoder_1_out11),
    .out12(decoder_1_out12), .out13(decoder_1_out13), .out14(decoder_1_out14), .out15(decoder_1_out15),
    .sel(SELECT), .en(not_1_out));
  Register #(.width(16)) register_1 (.D(INPUT), .en(decoder_1_out0), .Q(register_1_q), .clk(CLOCK));  // open: clr
  Register #(.width(16)) register_2 (.D(INPUT), .en(decoder_1_out1), .Q(register_2_q), .clk(CLOCK));  // open: clr
  Register #(.width(16)) register_3 (.D(INPUT), .en(decoder_1_out2), .Q(register_3_q), .clk(CLOCK));  // open: clr
  Register #(.width(16)) register_4 (.D(INPUT), .en(decoder_1_out3), .Q(register_4_q), .clk(CLOCK));  // open: clr
  Register #(.width(16)) register_5 (.D(INPUT), .en(decoder_1_out4), .Q(register_5_q), .clk(CLOCK));  // open: clr
  Register #(.width(16)) register_6 (.D(INPUT), .en(decoder_1_out5), .Q(register_6_q), .clk(CLOCK));  // open: clr
  Register #(.width(16)) register_7 (.D(INPUT), .en(decoder_1_out6), .Q(register_7_q), .clk(CLOCK));  // open: clr
  Register #(.width(16)) register_8 (.D(INPUT), .en(decoder_1_out7), .Q(register_8_q), .clk(CLOCK));  // open: clr
  Register #(.width(16)) register_9 (.D(INPUT), .en(decoder_1_out8), .Q(register_9_q), .clk(CLOCK));  // open: clr
  Register #(.width(16)) register_10 (.D(INPUT), .en(decoder_1_out9), .Q(register_10_q), .clk(CLOCK));  // open: clr
  Register #(.width(16)) register_11 (.D(INPUT), .en(decoder_1_out10), .Q(register_11_q), .clk(CLOCK));  // open: clr
  Register #(.width(16)) register_12 (.D(INPUT), .en(decoder_1_out11), .Q(register_12_q), .clk(CLOCK));  // open: clr
  Register #(.width(16)) register_13 (.D(INPUT), .en(decoder_1_out12), .Q(register_13_q), .clk(CLOCK));  // open: clr
  Register #(.width(16)) register_14 (.D(INPUT), .en(decoder_1_out13), .Q(register_14_q), .clk(CLOCK));  // open: clr
  Register #(.width(16)) register_15 (.D(INPUT), .en(decoder_1_out14), .Q(register_15_q), .clk(CLOCK));  // open: clr
  Register #(.width(16)) register_16 (.D(INPUT), .en(decoder_1_out15), .Q(register_16_q), .clk(CLOCK));  // open: clr
  Multiplexer #(.select(4), .width(16)) multiplexer_1 (
    .in0(register_1_q), .in1(register_2_q), .in2(register_3_q), .in3(register_4_q), .in4(register_5_q),
    .in5(register_6_q), .in6(register_7_q), .in7(register_8_q), .in8(register_9_q), .in9(register_10_q),
    .in10(register_11_q), .in11(register_12_q), .in12(register_13_q), .in13(register_14_q),
    .in14(register_15_q), .in15(register_16_q), .out(OUTPUT), .sel(SELECT), .en(R_W_prime));
endmodule

module main2 (
);

  wire clock_1_out, shift_register_1_out;

  Clock clock_1 (.out(clock_1_out));
  Shift_Register shift_register_1 (
    .in(shift_register_1_out), .clk(clock_1_out), .out(shift_register_1_out));  // open: shift, load, clr, d0, q0, d1, q1, d2, q2, d3, q3, d4, q4, d5, q5, d6, q6, d7, q7
  Shifter shifter_1 ();  // open: in, dist, out
endmodule

module v1_1 (
  input  [8:0] in_1
);

  wire Clock_out, not_1_out, shift_register_1_out, shift_register_2_out, shift_register_3_out,
       shift_register_4_out, shift_register_5_out, undriven;
  wire [3:0] alu_1_p3, IR_q_2, IR_q_3, multiplexer_3_out;
  wire [7:0] IR_q, multiplexer_1_out, ram_1_data, register_1_q;
  wire [8:0] adder_1_out, MAR_q, PC_q;
  wire [15:0] alu_1_p1, alu_1_p4, bit_extender_1_out, register_2_q;
  wire [19:0] bit_extender_2_out, MDR_q, multiplexer_2_out, rom_1_data;

  Clock Clock (.out(Clock_out));
  Shift_Register #(.length(5)) shift_register_1 (
    .in(shift_register_1_out), .clk(Clock_out), .out(shift_register_1_out));  // open: shift, load, clr, d0, q0, d1, q1, d2, q2, d3, q3, d4, q4
  Shift_Register #(.length(5)) shift_register_2 (
    .in(shift_register_2_out), .clk(Clock_out), .out(shift_register_2_out));  // open: shift, load, clr, d0, q0, d1, q1, d2, q2, d3, q3, d4, q4
  Multiplexer #(.width(8)) multiplexer_1 (
    .in0(IR_q), .in1(register_1_q), .out(multiplexer_1_out), .sel(shift_register_2_out));  // open: en
  Shift_Register #(.length(5)) shift_register_3 (
    .in(shift_register_3_out), .clk(Clock_out), .out(shift_register_3_out));  // open: shift, load, clr, d0, q0, d1, q1, d2, q2, d3, q3, d4, q4
  Adder #(.width(9)) adder_1 (.a(in_1), .b(PC_q), .out(adder_1_out), .cin(shift_register_1_out));  // open: cout
  ROM #(.addrWidth(9), .dataWidth(20)) rom_1 (.addr(MAR_q), .data(rom_1_data));  // open: sel
  not not_1 (not_1_out, 1'b1);
  Register #(.width(9)) PC (.D(adder_1_out), .en(1'b1), .Q(PC_q), .clk(Clock_out));  // open: clr
  Multiplexer #(.width(20)) multiplexer_2 (
    .in0(rom_1_data), .in1(bit_extender_2_out), .out(multiplexer_2_out));  // open: sel, en
  Bit_Extender #(.in_width(16), .out_width(8)) bit_extender_1 (.in(register_2_q), .out(bit_extender_1_out[7:0]));
  Register #(.width(9)) MAR (.D(PC_q), .en(shift_register_3_out), .Q(MAR_q), .clk(Clock_out));  // open: clr
  RAM #(.bus("separate")) ram_1 (
    .addr(multiplexer_1_out), .data(ram_1_data), .str(not_1_out), .sel(1'b1), .clk(Clock_out), .ld(1'b1));  // open: din, clr
  Shift_Register #(.length(5)) shift_register_4 (
    .in(shift_register_4_out), .clk(Clock_out), .out(shift_register_4_out));  // open: shift, load, clr, d0, q0, d1, q1, d2, q2, d3, q3, d4, q4
  Register #(.width(20)) MDR (.D(multiplexer_2_out), .en(undriven), .Q(MDR_q), .clk(Clock_out));  // open: clr
  Shift_Register #(.length(5)) shift_register_5 (
    .in(shift_register_5_out), .clk(Clock_out), .out(shift_register_5_out));  // open: shift, load, clr, d0, q0, d1, q1, d2, q2, d3, q3, d4, q4
  assign bit_extender_2_out = {{12{1'b0}}, ram_1_data};  // Bit_Extender bit_extender_2
  Register register_1 (.en(1'b1), .Q(register_1_q), .clk(Clock_out));  // open: D, clr
  // alu alu_1: pin names not known; wires that end beside it: alu_1_p1, register_1_q, alu_1_p3, alu_1_p4
  register_file register_file_1 (
    .INPUT(bit_extender_1_out), .SELECT(multiplexer_3_out), .R_W_prime(shift_register_4_out),
    .CLOCK(Clock_out), .OUTPUT(alu_1_p1));
  Register #(.width(20)) IR (
    .en(shift_register_5_out), .Q({alu_1_p3, IR_q_3, IR_q_2, IR_q}), .clk(Clock_out));  // open: D, clr
  Register #(.width(16)) register_2 (.D(alu_1_p4), .en(1'b1), .Q(register_2_q), .clk(Clock_out));  // open: clr
  Multiplexer #(.width(4), .enable("false")) multiplexer_3 (
    .in0(IR_q_3), .in1(IR_q_2), .out(multiplexer_3_out), .sel(shift_register_4_out));
  // Pins of 8 and 16 bits meet at bit_extender_1_out

  // Notes on the sheet:
  //   contents of rom_1 (hex, n*v repeats v):
  //   21200 20202
endmodule

// PC
module pc (
  input  PcEnable,
  input  [8:0] PC_IN,
  input  pcReset,
  input  CLOCK,
  output [8:0] PC_OUT
);

  wire and_1_out, register_1_q;
  wire [8:0] multiplexer_1_out, register_2_q;

  Register #(.width(1)) register_1 (.D(1'b1), .en(1'b1), .Q(register_1_q), .clk(CLOCK), .clr(pcReset));
  and and_1 (and_1_out, register_1_q, PcEnable);
  Multiplexer #(.width(9), .enable("false")) multiplexer_1 (
    .in0(PC_IN), .in1({9{1'b0}}), .out(multiplexer_1_out), .sel(register_1_q));
  Adder #(.width(9)) adder_1 (.a(multiplexer_1_out), .b(register_2_q), .out(PC_OUT), .cin(and_1_out));  // open: cout
  Register #(.width(9)) register_2 (.D(PC_OUT), .en(1'b1), .Q(register_2_q), .clk(CLOCK), .clr(pcReset));
endmodule

module temp (
  input  [8:0] in_1,
  input  PcReset
);

  wire and_1_out, clock_1_out, load_exchange_1_load_exchangeop, nor_1_out, not_1_out, not_2_out, not_3_out,
       or_1_out, or_2_out, shift_register_1_out, shift_register_2_out, shift_register_2_q0,
       shift_register_3_out, shift_register_4_out, storecmp_1_storeop;
  wire [3:0] IR_q_2, multiplexer_2_out;
  wire [7:0] bit_extender_1_out, multiplexer_1_out;
  wire [8:0] MAR_q, pc_1_pc_out;
  wire [15:0] ALU_p1, bit_extender_2_out, IR_q, RA_q, ram_1_data, register_1_q, register_file_1_output;
  wire [19:0] MDR_q, rom_1_data;
  wire [31:0] ALU_p4, Rz_q;

  Clock clock_1 (.out(clock_1_out));
  Shift_Register #(.length(6)) shift_register_1 (
    .in(shift_register_1_out), .clk(clock_1_out), .out(shift_register_1_out));  // open: shift, load, clr, d0, q0, d1, q1, d2, q2, d3, q3, d4, q4, d5, q5
  Bit_Extender #(.in_width(16), .out_width(8)) bit_extender_1 (.in(register_1_q), .out(bit_extender_1_out));
  Shift_Register #(.length(6)) shift_register_2 (
    .in(shift_register_2_out), .clk(clock_1_out), .out(shift_register_2_out), .q0(shift_register_2_q0));  // open: shift, load, clr, d0, d1, q1, d2, q2, d3, q3, d4, q4, d5, q5
  Multiplexer #(.width(8)) multiplexer_1 (
    .in0(IR_q[7:0]), .in1(bit_extender_1_out), .out(multiplexer_1_out), .sel(shift_register_2_out));  // open: en
  Shift_Register #(.length(6)) shift_register_3 (
    .in(shift_register_3_out), .clk(clock_1_out), .out(shift_register_3_out));  // open: shift, load, clr, d0, q0, d1, q1, d2, q2, d3, q3, d4, q4, d5, q5
  pc pc_1 (.PcEnable(shift_register_1_out), .PC_IN(in_1), .CLOCK(clock_1_out), .pcReset(PcReset), .PC_OUT(pc_1_pc_out));
  ROM #(.addrWidth(9), .dataWidth(20)) rom_1 (.addr(MAR_q), .data(rom_1_data));  // open: sel
  not not_1 (not_1_out, or_2_out);
  Register #(.width(20)) MDR (.D(rom_1_data), .en(1'b1), .Q(MDR_q), .clk(clock_1_out), .clr(PcReset));
  storeCmp storecmp_1 (.OPCODE(IR_q_2), .storeOP(storecmp_1_storeop));
  Bit_Extender #(.in_width(32)) bit_extender_2 (.in(Rz_q), .out(bit_extender_2_out));
  Shift_Register #(.length(6)) shift_register_4 (
    .in(shift_register_4_out), .clk(clock_1_out), .out(shift_register_4_out));  // open: shift, load, clr, d0, q0, d1, q1, d2, q2, d3, q3, d4, q4, d5, q5
  Register #(.width(9)) MAR (.D(pc_1_pc_out), .en(shift_register_3_out), .Q(MAR_q), .clk(clock_1_out), .clr(PcReset));
  RAM #(.dataWidth(16), .bus("separate")) ram_1 (
    .addr(multiplexer_1_out), .din(ALU_p1), .data(ram_1_data), .str(not_1_out), .sel(1'b1),
    .clk(clock_1_out), .ld(or_2_out));  // open: clr
  Register #(.width(16)) RA (.D(register_1_q), .en(shift_register_2_q0), .Q(RA_q), .clk(clock_1_out));  // open: clr
  or or_1 (or_1_out, storecmp_1_storeop, shift_register_4_out);
  load_exchange load_exchange_1 (.OPCODE(IR_q_2), .load_exchangeOP(load_exchange_1_load_exchangeop));
  Register #(.width(20)) IR (.D(MDR_q), .en(1'b1), .Q({IR_q_2, IR_q}), .clk(clock_1_out), .clr(PcReset));
  Register #(.width(16)) register_1 (.D(ram_1_data), .en(1'b1), .Q(register_1_q), .clk(clock_1_out), .clr(PcReset));
  // alu ALU: pin names not known; wires that end beside it: ALU_p1, RA_q, IR_q_2, ALU_p4
  register_file register_file_1 (
    .INPUT(bit_extender_2_out), .SELECT(multiplexer_2_out), .R_W_prime(or_1_out), .CLOCK(clock_1_out),
    .OUTPUT(register_file_1_output));
  Register #(.width(16)) RB (
    .D(register_file_1_output), .en(shift_register_2_q0), .Q(ALU_p1), .clk(clock_1_out));  // open: clr
  Register #(.width(32)) Rz (.D(ALU_p4), .en(1'b1), .Q(Rz_q), .clk(clock_1_out));  // open: clr
  not not_2 (not_2_out, load_exchange_1_load_exchangeop);
  nor nor_1 (nor_1_out, storecmp_1_storeop, not_3_out);
  Multiplexer #(.width(4), .enable("false")) multiplexer_2 (
    .in0(IR_q[15:12]), .in1(IR_q[11:8]), .out(multiplexer_2_out), .sel(nor_1_out));
  or or_2 (or_2_out, not_2_out, shift_register_4_out);
  not not_3 (not_3_out, and_1_out);
  and and_1 (and_1_out, shift_register_4_out, not_2_out);

  // Notes on the sheet:
  //   contents of rom_1 (hex, n*v repeats v):
  //   23202 20202 22001
endmodule

// Ld/exc
module load_exchange (
  input  [3:0] OPCODE,
  output load_exchangeOP
);

  wire comparator_1_eq, comparator_2_eq;

  Comparator #(.width(4)) comparator_1 (.a(OPCODE), .b(4'b0001), .eq(comparator_1_eq));  // open: gt, lt
  Comparator #(.width(4)) comparator_2 (.a(OPCODE), .b(4'b1011), .eq(comparator_2_eq));  // open: gt, lt
  or or_1 (load_exchangeOP, comparator_1_eq, comparator_2_eq);
endmodule

// sCmp
module storeCmp (
  input  [3:0] OPCODE,
  output storeOP
);

  Comparator #(.width(4)) comparator_1 (.a(OPCODE), .b(4'b0001), .eq(storeOP));  // open: gt, lt
endmodule

module PSW (
  input  [31:0] INPUT,
  output CARRY,
  output NEGATIVE,
  output OVERFLOW,
  output POSITIVE,
  output ZERO,
  output EVEN_PARITY,
  output ODD_PARITY
);

  wire or_2_out, or_3_out;

  xor odd_parity_1 (ODD_PARITY, INPUT[0], INPUT[1], INPUT[2], INPUT[3], INPUT[4], INPUT[5], INPUT[6], INPUT[7], INPUT[8], INPUT[9], INPUT[10], INPUT[11], INPUT[12], INPUT[13], INPUT[14], INPUT[15], INPUT[16], INPUT[17], INPUT[18], INPUT[19], INPUT[20], INPUT[21], INPUT[22], INPUT[23], INPUT[24], INPUT[25], INPUT[26], INPUT[27], INPUT[28], INPUT[29], INPUT[30], INPUT[31]);
  or or_1 (OVERFLOW, INPUT[31], INPUT[30], INPUT[29], INPUT[28], INPUT[27], INPUT[26], INPUT[25], INPUT[24], INPUT[23], INPUT[22], INPUT[21], INPUT[20], INPUT[19], INPUT[18], INPUT[17], INPUT[16]);
  not not_1 (EVEN_PARITY, ODD_PARITY);
  or or_2 (or_2_out, OVERFLOW, or_3_out);
  not not_2 (ZERO, or_2_out);
  or or_3 (or_3_out, INPUT[15], INPUT[14], INPUT[13], INPUT[12], INPUT[11], INPUT[10], INPUT[9], INPUT[8], INPUT[7], INPUT[6], INPUT[5], INPUT[4], INPUT[3], INPUT[2], INPUT[1], INPUT[0]);
  not not_3 (POSITIVE, INPUT[15]);

  assign CARRY = INPUT[16];
  assign NEGATIVE = INPUT[15];
endmodule

module UI (
  input  [8:0] in_1,
  output [19:0] IR_BUFF,
  output [19:0] CM,
  output [19:0] MDR_OUT,
  output [19:0] IR_OUT,
  output [15:0] RB,
  output [15:0] TEMP_REG_DM,
  output [15:0] DATA_MEMORY,
  output [15:0] REG_FILE_OUT,
  output [15:0] RA,
  output [31:0] ALU_OUT,
  output [31:0] RZ,
  output [8:0] PC_OUT,
  output [8:0] MAR_OUT
);

  wire CARRY, CLOCK, EVEN_PARITY, NEGETIVE, ODD_PARITY, OVERFLOW, POSITIVE, ZERO;
  wire [3:0] bit_extender_1_out, bit_extender_2_out, bit_extender_3_out;

  Hex_Digit_Display hex_digit_display_1 (.value(bit_extender_1_out));  // open: dp
  assign bit_extender_1_out = {{3{1'b0}}, in_1[8]};  // Bit_Extender bit_extender_1
  Hex_Digit_Display hex_digit_display_2 (.value(in_1[7:4]));  // open: dp
  Hex_Digit_Display hex_digit_display_3 (.value(in_1[3:0]));  // open: dp
  Clock clock_1 (.out(CLOCK));
  Hex_Digit_Display hex_digit_display_4 (.value(IR_BUFF[19:16]));  // open: dp
  Hex_Digit_Display hex_digit_display_5 (.value(IR_BUFF[11:8]));  // open: dp
  Hex_Digit_Display hex_digit_display_6 (.value(IR_BUFF[15:12]));  // open: dp
  Hex_Digit_Display hex_digit_display_7 (.value(REG_FILE_OUT[15:12]));  // open: dp
  Hex_Digit_Display hex_digit_display_8 (.value(REG_FILE_OUT[11:8]));  // open: dp
  Hex_Digit_Display hex_digit_display_9 (.value(ALU_OUT[27:24]));  // open: dp
  Hex_Digit_Display hex_digit_display_10 (.value(ALU_OUT[31:28]));  // open: dp
  Hex_Digit_Display hex_digit_display_11 (.value(IR_BUFF[3:0]));  // open: dp
  Hex_Digit_Display hex_digit_display_12 (.value(IR_BUFF[7:4]));  // open: dp
  Hex_Digit_Display hex_digit_display_13 (.value(REG_FILE_OUT[3:0]));  // open: dp
  Hex_Digit_Display hex_digit_display_14 (.value(REG_FILE_OUT[7:4]));  // open: dp
  Hex_Digit_Display hex_digit_display_15 (.value(ALU_OUT[23:20]));  // open: dp
  Hex_Digit_Display hex_digit_display_16 (.value(ALU_OUT[19:16]));  // open: dp
  Hex_Digit_Display hex_digit_display_17 (.value(ALU_OUT[15:12]));  // open: dp
  Hex_Digit_Display hex_digit_display_18 (.value(ALU_OUT[11:8]));  // open: dp
  main main_1 (
    .PC_in(in_1), .CLOCK(CLOCK), .CARRY(CARRY), .NEGETIVE(NEGETIVE), .OVERFLOW(OVERFLOW), .POSTIVE(POSITIVE),
    .ZERO(ZERO), .EVEN_PARITY(EVEN_PARITY), .ODD_PARITY(ODD_PARITY), .MDR_OUT(MDR_OUT), .IR_OUT(IR_OUT),
    .MAR_OUT(MAR_OUT), .RA(RA), .PC_OUT(PC_OUT), .IR_BUFF(IR_BUFF), .RB(RB), .RZ(RZ), .ALU_OUT(ALU_OUT),
    .REG_FILE_OUT(REG_FILE_OUT), .TEMP_REG_DM(TEMP_REG_DM), .DATA_MEMORY(DATA_MEMORY), .RB_2(CM));  // open: PcReset
  Hex_Digit_Display hex_digit_display_19 (.value(MDR_OUT[19:16]));  // open: dp
  Hex_Digit_Display hex_digit_display_20 (.value(ALU_OUT[3:0]));  // open: dp
  Hex_Digit_Display hex_digit_display_21 (.value(ALU_OUT[7:4]));  // open: dp
  Hex_Digit_Display hex_digit_display_22 (.value(MDR_OUT[15:12]));  // open: dp
  Hex_Digit_Display hex_digit_display_23 (.value(MDR_OUT[11:8]));  // open: dp
  Hex_Digit_Display hex_digit_display_24 (.value(RA[15:12]));  // open: dp
  Hex_Digit_Display hex_digit_display_25 (.value(RA[11:8]));  // open: dp
  Hex_Digit_Display hex_digit_display_26 (.value(RZ[31:28]));  // open: dp
  Hex_Digit_Display hex_digit_display_27 (.value(MDR_OUT[7:4]));  // open: dp
  Hex_Digit_Display hex_digit_display_28 (.value(MDR_OUT[3:0]));  // open: dp
  Hex_Digit_Display hex_digit_display_29 (.value(RA[7:4]));  // open: dp
  Hex_Digit_Display hex_digit_display_30 (.value(RA[3:0]));  // open: dp
  Hex_Digit_Display hex_digit_display_31 (.value(RZ[27:24]));  // open: dp
  Hex_Digit_Display hex_digit_display_32 (.value(RZ[23:20]));  // open: dp
  Hex_Digit_Display hex_digit_display_33 (.value(RZ[15:12]));  // open: dp
  Hex_Digit_Display hex_digit_display_34 (.value(RZ[19:16]));  // open: dp
  Hex_Digit_Display hex_digit_display_35 (.value(IR_OUT[19:16]));  // open: dp
  Hex_Digit_Display hex_digit_display_36 (.value(RZ[7:4]));  // open: dp
  Hex_Digit_Display hex_digit_display_37 (.value(RZ[11:8]));  // open: dp
  Hex_Digit_Display hex_digit_display_38 (.value(IR_OUT[15:12]));  // open: dp
  Hex_Digit_Display hex_digit_display_39 (.value(IR_OUT[11:8]));  // open: dp
  Hex_Digit_Display hex_digit_display_40 (.value(TEMP_REG_DM[11:8]));  // open: dp
  Hex_Digit_Display hex_digit_display_41 (.value(TEMP_REG_DM[15:12]));  // open: dp
  Hex_Digit_Display hex_digit_display_42 (.value(RZ[3:0]));  // open: dp
  Hex_Digit_Display hex_digit_display_43 (.value(IR_OUT[3:0]));  // open: dp
  Hex_Digit_Display hex_digit_display_44 (.value(IR_OUT[7:4]));  // open: dp
  Hex_Digit_Display hex_digit_display_45 (.value(TEMP_REG_DM[7:4]));  // open: dp
  Hex_Digit_Display hex_digit_display_46 (.value(TEMP_REG_DM[3:0]));  // open: dp
  Hex_Digit_Display hex_digit_display_47 (.value(CM[19:16]));  // open: dp
  Hex_Digit_Display hex_digit_display_48 (.value(MAR_OUT[7:4]));  // open: dp
  Hex_Digit_Display hex_digit_display_49 (.value(bit_extender_2_out));  // open: dp
  assign bit_extender_2_out = {{3{1'b0}}, MAR_OUT[8]};  // Bit_Extender bit_extender_2
  Hex_Digit_Display hex_digit_display_50 (.value(CM[11:8]));  // open: dp
  Hex_Digit_Display hex_digit_display_51 (.value(CM[15:12]));  // open: dp
  Hex_Digit_Display hex_digit_display_52 (.value(MAR_OUT[3:0]));  // open: dp
  Hex_Digit_Display hex_digit_display_53 (.value(CM[3:0]));  // open: dp
  Hex_Digit_Display hex_digit_display_54 (.value(CM[7:4]));  // open: dp
  Hex_Digit_Display hex_digit_display_55 (.value(RB[15:12]));  // open: dp
  Hex_Digit_Display hex_digit_display_56 (.value(RB[11:8]));  // open: dp
  Hex_Digit_Display hex_digit_display_57 (.value(RB[3:0]));  // open: dp
  Hex_Digit_Display hex_digit_display_58 (.value(RB[7:4]));  // open: dp
  LED led_1 (.in(CARRY));
  LED led_2 (.in(NEGETIVE));
  LED led_3 (.in(OVERFLOW));
  LED led_4 (.in(POSITIVE));
  LED led_5 (.in(ZERO));
  LED led_6 (.in(EVEN_PARITY));
  LED led_7 (.in(ODD_PARITY));
  Hex_Digit_Display hex_digit_display_59 (.value(PC_OUT[7:4]));  // open: dp
  Hex_Digit_Display hex_digit_display_60 (.value(bit_extender_3_out));  // open: dp
  assign bit_extender_3_out = {{3{1'b0}}, PC_OUT[8]};  // Bit_Extender bit_extender_3
  Hex_Digit_Display hex_digit_display_61 (.value(DATA_MEMORY[11:8]));  // open: dp
  Hex_Digit_Display hex_digit_display_62 (.value(DATA_MEMORY[15:12]));  // open: dp
  Hex_Digit_Display hex_digit_display_63 (.value(PC_OUT[3:0]));  // open: dp
  Hex_Digit_Display hex_digit_display_64 (.value(DATA_MEMORY[3:0]));  // open: dp
  Hex_Digit_Display hex_digit_display_65 (.value(DATA_MEMORY[7:4]));  // open: dp

  // Other names for the same wires on the sheet: DM[15:0] = DATA_MEMORY; PC_IN[8:0] = in_1;
  //   TEMP_REG__dm[15:0] = TEMP_REG_DM

  // Notes on the sheet:
  //   0000 0x0 LOAD
  //   0001 0x1 STORE
  //   0010 0x2 ADD
  //   0011 0x3 Subtract
  //   0100 0x4 Multiply
  //   0101 0x5 Divide
  //   0110 0x6 Increment
  //   0111 0x7 Decrement
  //   1000 0x8 AND
  //   1001 0x9 OR
  //   1010 0xA NOT
  //   1011 0xB Exchange
  //   1100 0xC Left Shift
  //   1101 0xD Right Shift
  //   1110 0xE Rotate Left
  //   1111 0xF Rotate Right
endmodule
